# Fritzing sketch Verkabelung_Sensor (saved by Fritzing 0.9.6b)

parts:
  WeMos_D1_Mini1 = WeMos D1 Mini
  Bauteil1 = BME280 Breakout

nets:
  5V: WeMos_D1_Mini1.5V, Bauteil1.3.3V
  N1: WeMos_D1_Mini1.D1, Bauteil1.SCK/SCL
  N2: WeMos_D1_Mini1.D2, Bauteil1.SDI/SDA
  N3: WeMos_D1_Mini1.G, Bauteil1.GND
